# Fritzing sketch siguelineas (saved by Fritzing 0.9.2b)
circuit board: 9.94152cm x 6.49917cm

parts:
  TCRT1 = TCRT5000 [package="DIP (Dual Inline) [THT]"]
  TCRT2 = TCRT5000 [package="DIP (Dual Inline) [THT]"]
  M1 = DC Motor
  M2 = DC Motor
  S1 = Toggle Switch [package=THT]
  L1 = Driver_l9110 [package="DIP (Dual Inline) [THT]"]
  BAT1 = Battery Holders [package=battery-aa-kit]
  BAT2 = Battery Holders [package=battery-aa-kit]
  BAT3 = Battery Holders [package=battery-aa-kit]
  BAT4 = Battery Holders [package=battery-aa-kit]
  Componente1 = Arduino Nano (Rev3.0)
  U3 = HC-SR04 [chip_label=IC package="SIP (Single Inline) [THT]"]

nets:
  N1: TCRT1.5_V, TCRT2.5_V, Componente1.5V
  GND: TCRT1.GND, BAT1.+, BAT1.-, BAT2.-, Componente1.GND
  N2: TCRT1.DO, Componente1.A3
  N3: TCRT2.DO, Componente1.A1
  N4: M1.pin_1, L1.2
  N5: M1.pin_2, L1.1
  N6: M2.pin_1, L1.4
  N7: M2.pin_2, L1.3
  VCC: S1.COM, L1.VCC, Componente1.VIN
  N8: S1.L2, BAT4.+
  N9: L1.1B1, Componente1.D5
  N10: L1.1A1, Componente1.D6
  N11: L1.1B2, Componente1.D7
  N12: L1.1A2, Componente1.D8
  N13: BAT2.+, BAT3.-
  N14: BAT3.+, BAT4.-
  N15: Componente1.D9, U3.Trig
  N16: Componente1.D10, U3.Echo

notes:
  Motor Esquerdo
  Motor Dereito
  Pack baterias
  AA 2x2
  Driver motores l9110
  Sensores infrav.
  TCRT5000
  Arduino Nano
  Interruptor 2 posicións

custom parts:
  TCRT5000: Sensor infrarrojos
  Driver_l9110: Driver Arduino para motores
  HC-SR04: HC-SR04 ultrasound distance sensor
